# Fritzing sketch Sketch (saved by Fritzing 1.0.6)
breadboards: 1

parts:
  MH-ET_LIVE_ESP32_DEVKIT1 = MH-ET LIVE ESP32 DEVKIT 38 pins
  PIR1 = PIR sensor
  T1 = LM35 Temperature Sensor [package="TO92 [THT]"]

nets:
  N1: MH-ET_LIVE_ESP32_DEVKIT1.IO34, T1.Vout
  N2: MH-ET_LIVE_ESP32_DEVKIT1.IO12, PIR1.SIG
  GND: MH-ET_LIVE_ESP32_DEVKIT1.CMD, MH-ET_LIVE_ESP32_DEVKIT1.GND, PIR1.GND, T1.+Vs, T1.GND
  5V: MH-ET_LIVE_ESP32_DEVKIT1.5V, PIR1.VDD

custom parts:
  MH-ET LIVE ESP32 DEVKIT 38 pins: http://mh.nodebb.com/topic/2/mh-et-live-esp32-devkit
